// Logisim project stage1_to_3_circuit.circ as structural Verilog: 1 circuit, main circuit main
module main (
  input  in_1,
  input  in_2,
  input  in_3,
  input  in_4,
  input  in_5
);

  wire and_1_out, and_2_out, and_3_out, and_4_out, and_5_out, and_6_out, and_7_out, and_8_out, and_9_out,
       and_10_out, and_11_out, and_12_out, and_13_out, and_14_out, and_15_out, and_16_out, button_1_out,
       button_2_out, clock_1_out, j_k_ff_1_q, j_k_ff_2_q, j_k_ff_3_q, j_k_ff_4_q, j_k_ff_5_q, j_k_ff_6_q,
       j_k_ff_7_q, j_k_ff_8_q, j_k_ff_9_q, j_k_ff_10_q, j_k_ff_11_q, j_k_ff_12_q, not_1_out, or_1_out,
       or_2_out, or_3_out;
  wire [0:0] d_ff_5_q;
  wire [2:0] d_ff_10_q;
  wire [3:0] d_ff_1_q, d_ff_6_q;

  J_K_Flip_Flop j_k_ff_1 (.J(in_2), .K(in_2), .clk(or_2_out), .Q(j_k_ff_1_q));  // open: Qn, preset, reset
  J_K_Flip_Flop j_k_ff_2 (
    .J(j_k_ff_1_q), .K(j_k_ff_1_q), .clk(or_2_out), .Q(j_k_ff_2_q), .reset(or_1_out));  // open: Qn, preset
  J_K_Flip_Flop j_k_ff_3 (
    .J(and_1_out), .K(and_1_out), .clk(or_2_out), .Q(j_k_ff_3_q), .reset(or_1_out));  // open: Qn, preset
  J_K_Flip_Flop j_k_ff_4 (
    .J(and_2_out), .K(and_2_out), .clk(or_2_out), .Q(j_k_ff_4_q), .reset(or_1_out));  // open: Qn, preset
  LED led_1 (.in(j_k_ff_1_q));
  and and_1 (and_1_out, j_k_ff_1_q, j_k_ff_2_q);
  LED led_2 (.in(j_k_ff_2_q));
  and and_2 (and_2_out, and_1_out, j_k_ff_3_q);
  LED led_3 (.in(j_k_ff_3_q));
  LED led_4 (.in(j_k_ff_4_q));
  and and_3 (and_3_out, j_k_ff_4_q, j_k_ff_2_q);
  and and_4 (and_4_out, d_ff_1_q[0], d_ff_1_q[3]);
  or or_1 (or_1_out, and_3_out, and_5_out);
  J_K_Flip_Flop j_k_ff_5 (.J(in_2), .K(in_2), .clk(and_4_out), .Q(j_k_ff_5_q));  // open: Qn, preset, reset
  D_Flip_Flop d_ff_1 (.D(j_k_ff_1_q), .clk(and_7_out), .Q(d_ff_1_q[0]));  // open: Qn, preset, reset
  D_Flip_Flop d_ff_2 (.D(j_k_ff_2_q), .clk(and_7_out), .Q(d_ff_1_q[1]));  // open: Qn, preset, reset
  D_Flip_Flop d_ff_3 (.D(j_k_ff_3_q), .clk(and_7_out), .Q(d_ff_1_q[2]));  // open: Qn, preset, reset
  D_Flip_Flop d_ff_4 (.D(j_k_ff_4_q), .clk(and_7_out), .Q(d_ff_1_q[3]));  // open: Qn, preset, reset
  and and_5 (and_5_out, and_1_out, j_k_ff_5_q);
  LED led_5 (.in(j_k_ff_5_q));
  D_Flip_Flop d_ff_5 (.D(j_k_ff_5_q), .clk(or_2_out), .Q(d_ff_5_q[0]));  // open: Qn, preset, reset
  Hex_Digit_Display hex_digit_display_1 (.value({{3{in_3}}, d_ff_5_q[0]}));  // open: dp
  Hex_Digit_Display hex_digit_display_2 (.value(d_ff_1_q));  // open: dp
  Hex_Digit_Display hex_digit_display_3 (.value({in_5, d_ff_10_q}));  // open: dp
  or or_2 (or_2_out, and_11_out, and_15_out);
  Hex_Digit_Display hex_digit_display_4 (.value(d_ff_6_q));  // open: dp
  LED led_6 ();  // open: in
  Clock clock_1 (.out(clock_1_out));
  Button button_1 (.out(button_1_out));
  Button button_2 (.out(button_2_out));
  not not_1 (not_1_out, in_1);
  or or_3 (or_3_out, and_6_out, and_7_out);
  J_K_Flip_Flop j_k_ff_6 (.J(in_4), .K(in_4), .clk(or_3_out), .Q(j_k_ff_6_q), .reset(and_10_out));  // open: Qn, preset
  J_K_Flip_Flop j_k_ff_7 (
    .J(j_k_ff_6_q), .K(j_k_ff_6_q), .clk(or_3_out), .Q(j_k_ff_7_q), .reset(and_10_out));  // open: Qn, preset
  J_K_Flip_Flop j_k_ff_8 (
    .J(and_8_out), .K(and_8_out), .clk(or_3_out), .Q(j_k_ff_8_q), .reset(and_10_out));  // open: Qn, preset
  J_K_Flip_Flop j_k_ff_9 (
    .J(and_9_out), .K(and_9_out), .clk(or_3_out), .Q(j_k_ff_9_q), .reset(and_10_out));  // open: Qn, preset
  and and_6 (and_6_out, in_1, button_2_out);
  and and_7 (and_7_out, clock_1_out, not_1_out);
  LED led_7 (.in(j_k_ff_6_q));
  and and_8 (and_8_out, j_k_ff_6_q, j_k_ff_7_q);
  LED led_8 (.in(j_k_ff_7_q));
  LED led_9 (.in(j_k_ff_8_q));
  and and_9 (and_9_out, and_8_out, j_k_ff_8_q);
  LED led_10 (.in(j_k_ff_9_q));
  and and_10 (and_10_out, j_k_ff_9_q, j_k_ff_7_q);
  and and_11 (and_11_out, in_1, button_1_out);
  D_Flip_Flop d_ff_6 (.D(j_k_ff_6_q), .clk(or_3_out), .Q(d_ff_6_q[0]));  // open: Qn, preset, reset
  D_Flip_Flop d_ff_7 (.D(j_k_ff_7_q), .clk(or_3_out), .Q(d_ff_6_q[1]));  // open: Qn, preset, reset
  D_Flip_Flop d_ff_8 (.D(j_k_ff_8_q), .clk(or_3_out), .Q(d_ff_6_q[2]));  // open: Qn, preset, reset
  D_Flip_Flop d_ff_9 (.D(j_k_ff_9_q), .clk(or_3_out), .Q(d_ff_6_q[3]));  // open: Qn, preset, reset
  and and_12 (and_12_out, d_ff_6_q[0], d_ff_6_q[3]);
  J_K_Flip_Flop j_k_ff_10 (
    .J(in_4), .K(in_4), .clk(and_12_out), .Q(j_k_ff_10_q), .reset(and_14_out));  // open: Qn, preset
  J_K_Flip_Flop j_k_ff_11 (
    .J(j_k_ff_10_q), .K(j_k_ff_10_q), .clk(and_12_out), .Q(j_k_ff_11_q), .reset(and_14_out));  // open: Qn, preset
  J_K_Flip_Flop j_k_ff_12 (
    .J(and_13_out), .K(and_13_out), .clk(and_12_out), .Q(j_k_ff_12_q), .reset(and_14_out));  // open: Qn, preset
  LED led_11 (.in(j_k_ff_10_q));
  and and_13 (and_13_out, j_k_ff_10_q, j_k_ff_11_q);
  LED led_12 (.in(j_k_ff_11_q));
  LED led_13 (.in(j_k_ff_12_q));
  and and_14 (and_14_out, j_k_ff_12_q, j_k_ff_11_q);
  and and_15 (and_15_out, and_12_out, and_16_out);
  D_Flip_Flop d_ff_10 (.D(j_k_ff_10_q), .clk(or_3_out), .Q(d_ff_10_q[0]));  // open: Qn, preset, reset
  D_Flip_Flop d_ff_11 (.D(j_k_ff_11_q), .clk(or_3_out), .Q(d_ff_10_q[1]));  // open: Qn, preset, reset
  D_Flip_Flop d_ff_12 (.D(j_k_ff_12_q), .clk(or_3_out), .Q(d_ff_10_q[2]));  // open: Qn, preset, reset
  and and_16 (and_16_out, d_ff_10_q[2], d_ff_10_q[0]);

  // Notes on the sheet:
  //   UNITS FOR HOURS
  //   1
  //   2
  //   4
  //   8
  //   HOURS COUNTER
  //   TENS FOR HOURS
  //   HOURS
  //   MINUTES
  //   AM / PM
  //   turns on if pm
  //   clock
  //   set time mode
  //   hours +
  //   minutes +
  //   UNITS COLUMN FOR MINUTES
  //   1
  //   2
  //   4
  //   8
  //   MINUTES COUNTER
  //   if minutes =  60  then it will increament by 1 on the hours counter
  //   TENS COLUMN FOR MINUTES
  //   1
  //   2
  //   4
endmodule
