// Logisim project stage_1_clock_circuit.circ as structural Verilog: 1 circuit, main circuit main
module main (
  input  in_1,
  input  UNIT_COLUMN,
  input  in_3
);

  wire and_1_out, and_2_out, and_3_out, and_4_out, and_5_out, and_6_out, clock_1_out, j_k_ff_1_q, j_k_ff_2_q,
       j_k_ff_3_q, j_k_ff_4_q, j_k_ff_5_q, j_k_ff_6_q, j_k_ff_7_q;
  wire [2:0] d_ff_1_q;
  wire [3:0] d_ff_4_q;

  J_K_Flip_Flop j_k_ff_1 (.J(in_1), .K(in_1), .clk(and_3_out), .Q(j_k_ff_1_q), .reset(and_2_out));  // open: Qn, preset
  LED led_1 (.in(j_k_ff_1_q));
  D_Flip_Flop d_ff_1 (.D(j_k_ff_1_q), .clk(clock_1_out), .Q(d_ff_1_q[0]));  // open: Qn, preset, reset
  J_K_Flip_Flop j_k_ff_2 (
    .J(j_k_ff_1_q), .K(j_k_ff_1_q), .clk(and_3_out), .Q(j_k_ff_2_q), .reset(and_2_out));  // open: Qn, preset
  LED led_2 (.in(j_k_ff_2_q));
  D_Flip_Flop d_ff_2 (.D(j_k_ff_2_q), .clk(clock_1_out), .Q(d_ff_1_q[1]));  // open: Qn, preset, reset
  and and_1 (and_1_out, j_k_ff_1_q, j_k_ff_2_q);
  J_K_Flip_Flop j_k_ff_3 (
    .J(and_1_out), .K(and_1_out), .clk(and_3_out), .Q(j_k_ff_3_q), .reset(and_2_out));  // open: Qn, preset
  D_Flip_Flop d_ff_3 (.D(j_k_ff_3_q), .clk(clock_1_out), .Q(d_ff_1_q[2]));  // open: Qn, preset, reset
  LED led_3 (.in(j_k_ff_3_q));
  and and_2 (and_2_out, j_k_ff_2_q, j_k_ff_3_q);
  and and_3 (and_3_out, d_ff_4_q[0], d_ff_4_q[3]);
  Clock clock_1 (.out(clock_1_out));
  Hex_Digit_Display hex_digit_display_1 (.value({in_3, d_ff_1_q}));  // open: dp
  Hex_Digit_Display hex_digit_display_2 (.value(d_ff_4_q));  // open: dp
  J_K_Flip_Flop j_k_ff_4 (
    .J(UNIT_COLUMN), .K(UNIT_COLUMN), .clk(clock_1_out), .Q(j_k_ff_4_q), .reset(and_6_out));  // open: Qn, preset
  LED led_4 (.in(j_k_ff_4_q));
  D_Flip_Flop d_ff_4 (.D(j_k_ff_4_q), .clk(clock_1_out), .Q(d_ff_4_q[0]));  // open: Qn, preset, reset
  J_K_Flip_Flop j_k_ff_5 (
    .J(j_k_ff_4_q), .K(j_k_ff_4_q), .clk(clock_1_out), .Q(j_k_ff_5_q), .reset(and_6_out));  // open: Qn, preset
  LED led_5 (.in(j_k_ff_5_q));
  D_Flip_Flop d_ff_5 (.D(j_k_ff_5_q), .clk(clock_1_out), .Q(d_ff_4_q[1]));  // open: Qn, preset, reset
  and and_4 (and_4_out, j_k_ff_4_q, j_k_ff_5_q);
  J_K_Flip_Flop j_k_ff_6 (
    .J(and_4_out), .K(and_4_out), .clk(clock_1_out), .Q(j_k_ff_6_q), .reset(and_6_out));  // open: Qn, preset
  LED led_6 (.in(j_k_ff_6_q));
  D_Flip_Flop d_ff_6 (.D(j_k_ff_6_q), .clk(clock_1_out), .Q(d_ff_4_q[2]));  // open: Qn, preset, reset
  and and_5 (and_5_out, and_4_out, j_k_ff_6_q);
  J_K_Flip_Flop j_k_ff_7 (
    .J(and_5_out), .K(and_5_out), .clk(clock_1_out), .Q(j_k_ff_7_q), .reset(and_6_out));  // open: Qn, preset
  and and_6 (and_6_out, j_k_ff_5_q, j_k_ff_7_q);
  D_Flip_Flop d_ff_7 (.D(j_k_ff_7_q), .clk(clock_1_out), .Q(d_ff_4_q[3]));  // open: Qn, preset, reset
  LED led_7 (.in(j_k_ff_7_q));

  // Notes on the sheet:
  //   TENS COLUMN
  //   1
  //   2
  //   4
  //   MINUTES
  //   1
  //   2
  //   4
  //   8
endmodule
