// Logisim project stage_2_clock_circuit.circ as structural Verilog: 1 circuit, main circuit main
module main (
  input  in_1,
  input  in_2,
  input  in_3,
  input  in_4
);

  wire and_1_out, and_2_out, and_3_out, and_4_out, and_5_out, and_6_out, and_7_out, and_8_out, button_1_out,
       clock_1_out, j_k_ff_1_q, j_k_ff_2_q, j_k_ff_3_q, j_k_ff_4_q, j_k_ff_5_q, j_k_ff_6_q, j_k_ff_7_q,
       not_1_out, or_1_out;
  wire [2:0] d_ff_1_q;
  wire [3:0] d_ff_4_q;

  J_K_Flip_Flop j_k_ff_1 (.J(in_2), .K(in_2), .clk(and_3_out), .Q(j_k_ff_1_q), .reset(and_2_out));  // open: Qn, preset
  D_Flip_Flop d_ff_1 (.D(j_k_ff_1_q), .clk(or_1_out), .Q(d_ff_1_q[0]));  // open: Qn, preset, reset
  LED led_1 (.in(j_k_ff_1_q));
  J_K_Flip_Flop j_k_ff_2 (
    .J(j_k_ff_1_q), .K(j_k_ff_1_q), .clk(and_3_out), .Q(j_k_ff_2_q), .reset(and_2_out));  // open: Qn, preset
  D_Flip_Flop d_ff_2 (.D(j_k_ff_2_q), .clk(or_1_out), .Q(d_ff_1_q[1]));  // open: Qn, preset, reset
  and and_1 (and_1_out, j_k_ff_1_q, j_k_ff_2_q);
  LED led_2 (.in(j_k_ff_2_q));
  J_K_Flip_Flop j_k_ff_3 (
    .J(and_1_out), .K(and_1_out), .clk(and_3_out), .Q(j_k_ff_3_q), .reset(and_2_out));  // open: Qn, preset
  D_Flip_Flop d_ff_3 (.D(j_k_ff_3_q), .clk(or_1_out), .Q(d_ff_1_q[2]));  // open: Qn, preset, reset
  LED led_3 (.in(j_k_ff_3_q));
  and and_2 (and_2_out, j_k_ff_2_q, j_k_ff_3_q);
  and and_3 (and_3_out, d_ff_4_q[0], d_ff_4_q[3]);
  Clock clock_1 (.out(clock_1_out));
  and and_4 (and_4_out, clock_1_out, not_1_out);
  not not_1 (not_1_out, in_1);
  or or_1 (or_1_out, and_4_out, and_5_out);
  Hex_Digit_Display hex_digit_display_1 (.value({in_4, d_ff_1_q}));  // open: dp
  J_K_Flip_Flop j_k_ff_4 (.J(in_3), .K(in_3), .clk(or_1_out), .Q(j_k_ff_4_q), .reset(and_8_out));  // open: Qn, preset
  Hex_Digit_Display hex_digit_display_2 (.value(d_ff_4_q));  // open: dp
  Button button_1 (.out(button_1_out));
  and and_5 (and_5_out, clock_1_out, button_1_out);
  LED led_4 (.in(j_k_ff_4_q));
  D_Flip_Flop d_ff_4 (.D(j_k_ff_4_q), .clk(or_1_out), .Q(d_ff_4_q[0]));  // open: Qn, preset, reset
  J_K_Flip_Flop j_k_ff_5 (
    .J(j_k_ff_4_q), .K(j_k_ff_4_q), .clk(or_1_out), .Q(j_k_ff_5_q), .reset(and_8_out));  // open: Qn, preset
  D_Flip_Flop d_ff_5 (.D(j_k_ff_5_q), .clk(or_1_out), .Q(d_ff_4_q[1]));  // open: Qn, preset, reset
  and and_6 (and_6_out, j_k_ff_4_q, j_k_ff_5_q);
  LED led_5 (.in(j_k_ff_5_q));
  J_K_Flip_Flop j_k_ff_6 (
    .J(and_6_out), .K(and_6_out), .clk(or_1_out), .Q(j_k_ff_6_q), .reset(and_8_out));  // open: Qn, preset
  D_Flip_Flop d_ff_6 (.D(j_k_ff_6_q), .clk(or_1_out), .Q(d_ff_4_q[2]));  // open: Qn, preset, reset
  and and_7 (and_7_out, and_6_out, j_k_ff_6_q);
  LED led_6 (.in(j_k_ff_6_q));
  J_K_Flip_Flop j_k_ff_7 (
    .J(and_7_out), .K(and_7_out), .clk(or_1_out), .Q(j_k_ff_7_q), .reset(and_8_out));  // open: Qn, preset
  and and_8 (and_8_out, j_k_ff_5_q, j_k_ff_7_q);
  D_Flip_Flop d_ff_7 (.D(j_k_ff_7_q), .clk(or_1_out), .Q(d_ff_4_q[3]));  // open: Qn, preset, reset
  LED led_7 (.in(j_k_ff_7_q));

  // Notes on the sheet:
  //   1
  //   TENS COLUMN
  //   2
  //   4
  //   set time mode
  //   +m
  //   MINUTES
  //   1
  //   UNIT COLUMN
  //   2
  //   4
  //   8
endmodule
