// Logisim project stage_3_clock_circuit.circ as structural Verilog: 1 circuit, main circuit main
module main (
  input  HOUR_TEN,
  input  in_2,
  input  in_3,
  input  in_4,
  input  in_5,
  input  in_6,
  input  in_7,
  input  in_8,
  input  in_9
);

  wire and_1_out, and_2_out, and_3_out, and_4_out, and_5_out, and_6_out, and_7_out, and_8_out, and_9_out,
       and_10_out, and_11_out, and_12_out, and_13_out, button_1_out, clock_1_out, clock_2_out, j_k_ff_1_q,
       j_k_ff_2_q, j_k_ff_3_q, j_k_ff_4_q, j_k_ff_5_q, j_k_ff_6_q, j_k_ff_7_q, j_k_ff_8_q, j_k_ff_9_q,
       j_k_ff_10_q, j_k_ff_11_q, j_k_ff_12_q, not_1_out, or_1_out, or_2_out;
  wire [0:0] d_ff_2_q;
  wire [2:0] d_ff_6_q;
  wire [3:0] d_ff_1_q, d_ff_9_q;

  Clock clock_1 (.out(clock_1_out));
  J_K_Flip_Flop j_k_ff_1 (.J(in_5), .K(in_5), .clk(clock_1_out), .Q(j_k_ff_1_q));  // open: Qn, preset, reset
  D_Flip_Flop d_ff_1 (.D(j_k_ff_1_q), .clk(clock_1_out), .Q(d_ff_1_q[0]));  // open: Qn, preset, reset
  J_K_Flip_Flop j_k_ff_2 (
    .J(HOUR_TEN), .K(HOUR_TEN), .clk(and_3_out), .Q(j_k_ff_2_q), .reset(and_4_out));  // open: Qn, preset
  LED led_1 (.in(j_k_ff_1_q));
  LED led_2 (.in(j_k_ff_2_q));
  D_Flip_Flop d_ff_2 (.D(j_k_ff_2_q), .clk(clock_1_out), .Q(d_ff_2_q[0]));  // open: Qn, preset, reset
  J_K_Flip_Flop j_k_ff_3 (
    .J(j_k_ff_1_q), .K(j_k_ff_1_q), .clk(clock_1_out), .Q(j_k_ff_3_q), .reset(or_1_out));  // open: Qn, preset
  D_Flip_Flop d_ff_3 (.D(j_k_ff_3_q), .clk(clock_1_out), .Q(d_ff_1_q[1]));  // open: Qn, preset, reset
  and and_1 (and_1_out, j_k_ff_1_q, j_k_ff_3_q);
  LED led_3 (.in(j_k_ff_3_q));
  J_K_Flip_Flop j_k_ff_4 (
    .J(and_1_out), .K(and_1_out), .clk(clock_1_out), .Q(j_k_ff_4_q), .reset(or_1_out));  // open: Qn, preset
  D_Flip_Flop d_ff_4 (.D(j_k_ff_4_q), .clk(clock_1_out), .Q(d_ff_1_q[2]));  // open: Qn, preset, reset
  LED led_4 (.in(j_k_ff_4_q));
  D_Flip_Flop d_ff_5 (.D(j_k_ff_5_q), .clk(clock_1_out), .Q(d_ff_1_q[3]));  // open: Qn, preset, reset
  and and_2 (and_2_out, and_1_out, j_k_ff_4_q);
  J_K_Flip_Flop j_k_ff_5 (
    .J(and_2_out), .K(and_2_out), .clk(clock_1_out), .Q(j_k_ff_5_q), .reset(or_1_out));  // open: Qn, preset
  LED led_5 (.in(j_k_ff_5_q));
  and and_3 (and_3_out, d_ff_1_q[0], d_ff_1_q[3]);
  and and_4 (and_4_out, j_k_ff_2_q, and_1_out);
  and and_5 (and_5_out, j_k_ff_5_q, j_k_ff_3_q);
  or or_1 (or_1_out, and_4_out, and_5_out);
  Hex_Digit_Display hex_digit_display_1 (.value({in_2, in_3, in_4, d_ff_2_q[0]}));  // open: dp
  Hex_Digit_Display hex_digit_display_2 (.value(d_ff_1_q));  // open: dp
  J_K_Flip_Flop j_k_ff_6 (.J(in_7), .K(in_7), .clk(and_8_out), .Q(j_k_ff_6_q), .reset(and_7_out));  // open: Qn, preset
  D_Flip_Flop d_ff_6 (.D(j_k_ff_6_q), .clk(or_2_out), .Q(d_ff_6_q[0]));  // open: Qn, preset, reset
  LED led_6 (.in(j_k_ff_6_q));
  J_K_Flip_Flop j_k_ff_7 (
    .J(j_k_ff_6_q), .K(j_k_ff_6_q), .clk(and_8_out), .Q(j_k_ff_7_q), .reset(and_7_out));  // open: Qn, preset
  LED led_7 (.in(j_k_ff_7_q));
  D_Flip_Flop d_ff_7 (.D(j_k_ff_7_q), .clk(or_2_out), .Q(d_ff_6_q[1]));  // open: Qn, preset, reset
  and and_6 (and_6_out, j_k_ff_6_q, j_k_ff_7_q);
  J_K_Flip_Flop j_k_ff_8 (
    .J(and_6_out), .K(and_6_out), .clk(and_8_out), .Q(j_k_ff_8_q), .reset(and_7_out));  // open: Qn, preset
  LED led_8 (.in(j_k_ff_8_q));
  D_Flip_Flop d_ff_8 (.D(j_k_ff_8_q), .clk(or_2_out), .Q(d_ff_6_q[2]));  // open: Qn, preset, reset
  and and_7 (and_7_out, j_k_ff_7_q, j_k_ff_8_q);
  and and_8 (and_8_out, d_ff_9_q[0], d_ff_9_q[3]);
  Clock clock_2 (.out(clock_2_out));
  not not_1 (not_1_out, in_6);
  and and_9 (and_9_out, clock_2_out, not_1_out);
  or or_2 (or_2_out, and_9_out, and_10_out);
  Hex_Digit_Display hex_digit_display_3 (.value({in_9, d_ff_6_q}));  // open: dp
  Hex_Digit_Display hex_digit_display_4 (.value(d_ff_9_q));  // open: dp
  Button button_1 (.out(button_1_out));
  and and_10 (and_10_out, clock_2_out, button_1_out);
  J_K_Flip_Flop j_k_ff_9 (.J(in_8), .K(in_8), .clk(or_2_out), .Q(j_k_ff_9_q), .reset(and_13_out));  // open: Qn, preset
  LED led_9 (.in(j_k_ff_9_q));
  D_Flip_Flop d_ff_9 (.D(j_k_ff_9_q), .clk(or_2_out), .Q(d_ff_9_q[0]));  // open: Qn, preset, reset
  J_K_Flip_Flop j_k_ff_10 (
    .J(j_k_ff_9_q), .K(j_k_ff_9_q), .clk(or_2_out), .Q(j_k_ff_10_q), .reset(and_13_out));  // open: Qn, preset
  LED led_10 (.in(j_k_ff_10_q));
  D_Flip_Flop d_ff_10 (.D(j_k_ff_10_q), .clk(or_2_out), .Q(d_ff_9_q[1]));  // open: Qn, preset, reset
  and and_11 (and_11_out, j_k_ff_9_q, j_k_ff_10_q);
  J_K_Flip_Flop j_k_ff_11 (
    .J(and_11_out), .K(and_11_out), .clk(or_2_out), .Q(j_k_ff_11_q), .reset(and_13_out));  // open: Qn, preset
  LED led_11 (.in(j_k_ff_11_q));
  D_Flip_Flop d_ff_11 (.D(j_k_ff_11_q), .clk(or_2_out), .Q(d_ff_9_q[2]));  // open: Qn, preset, reset
  and and_12 (and_12_out, and_11_out, j_k_ff_11_q);
  J_K_Flip_Flop j_k_ff_12 (
    .J(and_12_out), .K(and_12_out), .clk(or_2_out), .Q(j_k_ff_12_q), .reset(and_13_out));  // open: Qn, preset
  LED led_12 (.in(j_k_ff_12_q));
  and and_13 (and_13_out, j_k_ff_10_q, j_k_ff_12_q);
  D_Flip_Flop d_ff_12 (.D(j_k_ff_12_q), .clk(or_2_out), .Q(d_ff_9_q[3]));  // open: Qn, preset, reset

  // Notes on the sheet:
  //   HOUR UNIT
  //   1
  //   1
  //   2
  //   4
  //   8
  //   TENS COLUMN
  //   1
  //   2
  //   4
  //   set time mode
  //   +m
  //   MINUTES
  //   1
  //   UNIT COLUMN
  //   2
  //   4
  //   8
endmodule
