// Logisim project NAND_GATE.circ as structural Verilog: 1 circuit, main circuit main
module main (
  input  pin_1,
  input  pin_2
);

  wire nand_1_out;

  nand nand_1 (nand_1_out, pin_1, pin_2);
  LED led_1 (.in(nand_1_out));

  // Notes on the sheet:
  //   sum
endmodule
