// Logisim project FlipFlop.circ as structural Verilog: 1 circuit, main circuit main
module main (
  input  set,
  input  reset
);

  wire nor_1_out, nor_2_out;

  nor nor_1 (nor_1_out, set, nor_2_out);
  nor nor_2 (nor_2_out, nor_1_out, reset);
  LED led_1 (.in(nor_1_out));
  LED led_2 (.in(nor_2_out));

  // Notes on the sheet:
  //   Q
  //   Q'
endmodule
