// Logisim project JK_FlipFlop.circ as structural Verilog: 1 circuit, main circuit main
module main (
  input  J,
  input  K,
  input  in_3,
  input  in_4
);

  wire j_k_ff_1_q, j_k_ff_1_qn, nand_1_out, nand_2_out, nand_3_out, nand_4_out;

  Clock clock_1 (.out(K));
  nand nand_1 (nand_1_out, nand_4_out, K);
  nand nand_2 (nand_2_out, K, nand_3_out);
  J_K_Flip_Flop j_k_ff_1 (.J(in_3), .K(K), .clk(in_4), .Q(j_k_ff_1_q), .Qn(j_k_ff_1_qn));  // open: preset, reset
  LED led_1 (.in(j_k_ff_1_q));
  LED led_2 (.in(j_k_ff_1_qn));
  nand nand_3 (nand_3_out, nand_1_out, nand_4_out);
  nand nand_4 (nand_4_out, nand_3_out, nand_2_out);
  LED led_3 (.in(nand_3_out));
  LED led_4 (.in(nand_4_out));

  // Notes on the sheet:
  //   clock
endmodule
