// Logisim project Common_Clock.circ as structural Verilog: 1 circuit, main circuit main
module main (
  input  in_1,
  input  in_2,
  input  in_3,
  input  in_4,
  input  in_5
);

  wire and_1_out, and_2_out, and_3_out, and_4_out, and_5_out, clock_1_out, clock_2_out, clock_3_out,
       j_k_ff_1_q, j_k_ff_3_q, j_k_ff_4_q, j_k_ff_6_q, j_k_ff_7_q, j_k_ff_9_q;
  wire [2:0] d_ff_1_q, j_k_ff_2_q;

  Clock clock_1 (.out(clock_1_out));
  Clock clock_2 (.out(clock_2_out));
  Clock clock_3 (.out(clock_3_out));
  J_K_Flip_Flop j_k_ff_1 (.J(in_1), .K(in_1), .clk(clock_1_out), .Q(j_k_ff_1_q));  // open: Qn, preset, reset
  J_K_Flip_Flop j_k_ff_2 (
    .J(in_2), .K(in_2), .clk(clock_2_out), .Q(j_k_ff_2_q[0]), .reset(and_4_out));  // open: Qn, preset
  LED led_1 (.in(j_k_ff_1_q));
  LED led_2 (.in(j_k_ff_2_q[0]));
  J_K_Flip_Flop j_k_ff_3 (
    .J(in_4), .K(in_4), .clk(clock_3_out), .Q(j_k_ff_3_q), .reset(and_5_out));  // open: Qn, preset
  LED led_3 (.in(j_k_ff_3_q));
  J_K_Flip_Flop j_k_ff_4 (
    .J(j_k_ff_1_q), .K(j_k_ff_1_q), .clk(clock_1_out), .Q(j_k_ff_4_q));  // open: Qn, preset, reset
  J_K_Flip_Flop j_k_ff_5 (
    .J(j_k_ff_2_q[0]), .K(j_k_ff_2_q[0]), .clk(clock_2_out), .Q(j_k_ff_2_q[1]), .reset(and_4_out));  // open: Qn, preset
  D_Flip_Flop #(.trigger("falling")) d_ff_1 (
    .D(j_k_ff_3_q), .clk(clock_3_out), .Q(d_ff_1_q[0]));  // open: Qn, preset, reset
  and and_1 (and_1_out, j_k_ff_1_q, j_k_ff_4_q);
  LED led_4 (.in(j_k_ff_4_q));
  and and_2 (and_2_out, j_k_ff_2_q[0], j_k_ff_2_q[1]);
  LED led_5 (.in(j_k_ff_2_q[1]));
  and and_3 (and_3_out, j_k_ff_3_q, j_k_ff_6_q);
  J_K_Flip_Flop j_k_ff_6 (
    .J(j_k_ff_3_q), .K(j_k_ff_3_q), .clk(clock_3_out), .Q(j_k_ff_6_q), .reset(and_5_out));  // open: Qn, preset
  LED led_6 (.in(j_k_ff_6_q));
  J_K_Flip_Flop j_k_ff_7 (.J(and_1_out), .K(and_1_out), .clk(clock_1_out), .Q(j_k_ff_7_q));  // open: Qn, preset, reset
  J_K_Flip_Flop j_k_ff_8 (
    .J(and_2_out), .K(and_2_out), .clk(clock_2_out), .Q(j_k_ff_2_q[2]), .reset(and_4_out));  // open: Qn, preset
  Hex_Digit_Display hex_digit_display_1 (.value({in_3, j_k_ff_2_q}));  // open: dp
  D_Flip_Flop #(.trigger("falling")) d_ff_2 (
    .D(j_k_ff_6_q), .clk(clock_3_out), .Q(d_ff_1_q[1]));  // open: Qn, preset, reset
  LED led_7 (.in(j_k_ff_7_q));
  LED led_8 (.in(j_k_ff_2_q[2]));
  and and_4 (and_4_out, j_k_ff_2_q[2], j_k_ff_2_q[1]);
  J_K_Flip_Flop j_k_ff_9 (
    .J(and_3_out), .K(and_3_out), .clk(clock_3_out), .Q(j_k_ff_9_q), .reset(and_5_out));  // open: Qn, preset
  and and_5 (and_5_out, j_k_ff_9_q, j_k_ff_6_q);
  LED led_9 (.in(j_k_ff_9_q));
  D_Flip_Flop #(.trigger("falling")) d_ff_3 (
    .D(j_k_ff_9_q), .clk(clock_3_out), .Q(d_ff_1_q[2]));  // open: Qn, preset, reset
  Hex_Digit_Display hex_digit_display_2 (.value({in_5, d_ff_1_q}));  // open: dp
endmodule
