// Logisim project big_edian_3_bit_ripple.circ as structural Verilog: 1 circuit, main circuit main
module main (
  input  in_1,
  input  in_2
);

  wire clock_1_out, clock_2_out, j_k_ff_1_q, j_k_ff_2_q, j_k_ff_3_q, j_k_ff_4_q, j_k_ff_5_q, j_k_ff_6_q;

  Clock clock_1 (.out(clock_1_out));
  Clock clock_2 (.out(clock_2_out));
  J_K_Flip_Flop #(.trigger("falling")) j_k_ff_1 (
    .J(in_1), .K(in_1), .clk(clock_1_out), .Q(j_k_ff_1_q));  // open: Qn, preset, reset
  J_K_Flip_Flop j_k_ff_2 (.J(in_2), .K(in_2), .clk(clock_2_out), .Q(j_k_ff_2_q));  // open: Qn, preset, reset
  LED led_1 (.in(j_k_ff_1_q));
  LED led_2 (.in(j_k_ff_2_q));
  J_K_Flip_Flop #(.trigger("falling")) j_k_ff_3 (
    .J(in_1), .K(in_1), .clk(j_k_ff_1_q), .Q(j_k_ff_3_q));  // open: Qn, preset, reset
  J_K_Flip_Flop j_k_ff_4 (.J(in_2), .K(in_2), .clk(j_k_ff_2_q), .Q(j_k_ff_4_q));  // open: Qn, preset, reset
  LED led_3 (.in(j_k_ff_3_q));
  LED led_4 (.in(j_k_ff_4_q));
  J_K_Flip_Flop #(.trigger("falling")) j_k_ff_5 (
    .J(in_1), .K(in_1), .clk(j_k_ff_3_q), .Q(j_k_ff_5_q));  // open: Qn, preset, reset
  LED led_5 (.in(j_k_ff_5_q));
  J_K_Flip_Flop j_k_ff_6 (.J(in_2), .K(in_2), .clk(j_k_ff_4_q), .Q(j_k_ff_6_q));  // open: Qn, preset, reset
  LED led_6 (.in(j_k_ff_6_q));
endmodule
