// Logisim project 5bitshiftregister.circ as structural Verilog: 1 circuit, main circuit main
module main (
  input  Left___Right,
  input  Input,
  input  in_3,
  input  reset,
  input  stack_toggle,
  input  reset_2
);

  wire and_1_out, and_2_out, and_3_out, and_4_out, and_5_out, and_6_out, and_7_out, and_8_out, and_9_out,
       and_10_out, and_11_out, and_12_out, and_13_out, and_14_out, and_15_out, clock_1_out, d_ff_1_q,
       d_ff_2_q, d_ff_3_q, d_ff_4_q, d_ff_5_q, d_ff_6_q, d_ff_7_q, d_ff_8_q, d_ff_9_q, d_ff_10_q, not_1_out,
       or_1_out, or_2_out, or_3_out, or_4_out, or_5_out;

  Clock clock_1 (.out(clock_1_out));
  not not_1 (not_1_out, Left___Right);
  and and_1 (and_1_out, Left___Right, Input);
  or or_1 (or_1_out, and_1_out, and_2_out);
  and and_2 (and_2_out, not_1_out, d_ff_3_q);
  D_Flip_Flop #(.trigger("falling")) d_ff_1 (
    .D(or_1_out), .clk(clock_1_out), .Q(d_ff_1_q), .reset(reset));  // open: Qn, preset
  LED led_1 (.in(d_ff_1_q));
  and and_3 (and_3_out, d_ff_1_q, stack_toggle);
  D_Flip_Flop d_ff_2 (.D(and_3_out), .clk(stack_toggle), .Q(d_ff_2_q), .reset(reset_2));  // open: Qn, preset
  LED led_2 (.in(d_ff_2_q));
  and and_4 (and_4_out, Left___Right, d_ff_1_q);
  or or_2 (or_2_out, and_4_out, and_5_out);
  and and_5 (and_5_out, not_1_out, d_ff_5_q);
  D_Flip_Flop #(.trigger("falling")) d_ff_3 (
    .D(or_2_out), .clk(clock_1_out), .Q(d_ff_3_q), .reset(reset));  // open: Qn, preset
  LED led_3 (.in(d_ff_3_q));
  and and_6 (and_6_out, d_ff_3_q, stack_toggle);
  D_Flip_Flop d_ff_4 (.D(and_6_out), .clk(stack_toggle), .Q(d_ff_4_q), .reset(reset_2));  // open: Qn, preset
  and and_7 (and_7_out, Left___Right, d_ff_3_q);
  or or_3 (or_3_out, and_7_out, and_8_out);
  D_Flip_Flop #(.trigger("falling")) d_ff_5 (
    .D(or_3_out), .clk(clock_1_out), .Q(d_ff_5_q), .reset(reset));  // open: Qn, preset
  LED led_4 (.in(d_ff_4_q));
  and and_8 (and_8_out, not_1_out, d_ff_6_q);
  LED led_5 (.in(d_ff_5_q));
  and and_9 (and_9_out, Left___Right, d_ff_5_q);
  and and_10 (and_10_out, d_ff_5_q, stack_toggle);
  and and_11 (and_11_out, not_1_out, d_ff_8_q);
  or or_4 (or_4_out, and_9_out, and_11_out);
  D_Flip_Flop #(.trigger("falling")) d_ff_6 (
    .D(or_4_out), .clk(clock_1_out), .Q(d_ff_6_q), .reset(reset));  // open: Qn, preset
  D_Flip_Flop d_ff_7 (.D(and_10_out), .clk(stack_toggle), .Q(d_ff_7_q), .reset(reset_2));  // open: Qn, preset
  LED led_6 (.in(d_ff_6_q));
  LED led_7 (.in(d_ff_7_q));
  and and_12 (and_12_out, d_ff_6_q, stack_toggle);
  and and_13 (and_13_out, Left___Right, d_ff_6_q);
  or or_5 (or_5_out, and_13_out, and_14_out);
  D_Flip_Flop #(.trigger("falling")) d_ff_8 (
    .D(or_5_out), .clk(clock_1_out), .Q(d_ff_8_q), .reset(reset));  // open: Qn, preset
  D_Flip_Flop d_ff_9 (.D(and_12_out), .clk(stack_toggle), .Q(d_ff_9_q), .reset(reset_2));  // open: Qn, preset
  and and_14 (and_14_out, not_1_out, in_3);
  LED led_8 (.in(d_ff_8_q));
  LED led_9 (.in(d_ff_9_q));
  and and_15 (and_15_out, d_ff_8_q, stack_toggle);
  D_Flip_Flop d_ff_10 (.D(and_15_out), .clk(stack_toggle), .Q(d_ff_10_q), .reset(reset_2));  // open: Qn, preset
  LED led_10 (.in(d_ff_10_q));

  // Notes on the sheet:
  //   clock
endmodule
